// Logisim project CIRC1.circ as structural Verilog: 1 circuit, main circuit main
module main (
  input  A,
  input  B,
  input  C,
  input  D,
  input  E
);

  wire B_prime_out, C___D_out, C_prime_out, D_prime_out, nand_1_out, nand_2_out, nand_3_out, nand_4_out,
       nand_5_out, nand_6_out, nand_7_out, nand_8_out, nand_9_out, nand_10_out, nand_11_out, nand_12_out,
       nand_13_out, nand_14_out, nand_15_out, nand_16_out, nand_17_out, nand_18_out, nand_19_out,
       nand_20_out, nand_21_out, nand_22_out, nand_23_out, nand_24_out, nand_25_out, nand_26_out,
       nand_27_out, nand_28_out, nand_29_out;

  nand B_prime (B_prime_out, B, B);
  nand nand_1 (nand_1_out, C, C);
  nand nand_2 (nand_2_out, B_prime_out, nand_1_out);
  nand C_prime (C_prime_out, C, C);
  nand D_prime (D_prime_out, D, D);
  nand nand_3 (nand_3_out, nand_2_out, nand_2_out);
  nand nand_4 (nand_4_out, A, A);
  nand nand_5 (nand_5_out, D, D);
  nand nand_6 (nand_6_out, A, A);
  nand C___D (C___D_out, C_prime_out, D_prime_out);
  nand nand_7 (nand_7_out, nand_3_out, E);
  nand nand_8 (nand_8_out, nand_4_out, B);
  nand nand_9 (nand_9_out, nand_5_out, E);
  nand nand_10 (nand_10_out, nand_6_out, B);
  nand nand_11 (nand_11_out, C, D);
  nand nand_12 (nand_12_out, A, B);
  nand nand_13 (nand_13_out, D, E);
  nand nand_14 (nand_14_out, C___D_out, nand_7_out);
  nand nand_15 (nand_15_out, nand_8_out, nand_8_out);
  nand nand_16 (nand_16_out, nand_9_out, nand_9_out);
  nand nand_17 (nand_17_out, nand_10_out, nand_10_out);
  nand nand_18 (nand_18_out, nand_11_out, nand_11_out);
  nand nand_19 (nand_19_out, nand_12_out, nand_12_out);
  nand nand_20 (nand_20_out, nand_13_out, nand_13_out);
  nand nand_21 (nand_21_out, nand_14_out, nand_14_out);
  nand nand_22 (nand_22_out, nand_15_out, nand_16_out);
  nand nand_23 (nand_23_out, nand_17_out, nand_18_out);
  nand nand_24 (nand_24_out, nand_19_out, nand_20_out);
  nand nand_25 (nand_25_out, nand_21_out, nand_22_out);
  nand nand_26 (nand_26_out, nand_23_out, nand_24_out);
  nand nand_27 (nand_27_out, nand_25_out, nand_25_out);
  nand nand_28 (nand_28_out, nand_26_out, nand_26_out);
  nand nand_29 (nand_29_out, nand_27_out, nand_28_out);
  LED led_1 (.in(nand_29_out));
endmodule
